// Logisim project Up-Down_Decade_counter.circ as structural Verilog: 5 circuits, main circuit main
module main (
  input  Up1_down0,
  input  Clear,
  input  Clock,
  output A1_lsb,
  output [3:0] HEX,
  output A2,
  output A3,
  output A4_MSB
);

  wire and_1_out, and_2_out, and_3_out, and_4_out, and_5_out, and_6_out, Clear_out, j_k_ff_1_qn, j_k_ff_2_qn,
       j_k_ff_3_qn, not_1_out, or_1_out, or_2_out, or_3_out, or_4_out, or_5_out, or_6_out, or_7_out,
       Preset_out;

  not not_1 (not_1_out, Up1_down0);
  and and_1 (and_1_out, j_k_ff_1_qn, not_1_out);
  and and_2 (and_2_out, A1_lsb, Up1_down0);
  and and_3 (and_3_out, j_k_ff_2_qn, and_1_out);
  and and_4 (and_4_out, A3, and_6_out);
  and and_5 (and_5_out, j_k_ff_3_qn, and_3_out);
  or or_1 (or_1_out, Up1_down0, not_1_out);
  or or_2 (or_2_out, and_2_out, and_1_out);
  and and_6 (and_6_out, and_2_out, A2);
  or or_3 (or_3_out, and_6_out, and_3_out);
  or or_4 (or_4_out, and_4_out, and_5_out);
  or or_5 (or_5_out, Clear_out, Clear);
  J_K_Flip_Flop j_k_ff_1 (
    .J(or_1_out), .clk(Clock), .K(or_1_out), .Q(A1_lsb), .Qn(j_k_ff_1_qn), .preset(Preset_out),
    .reset(or_5_out));  // open: en
  J_K_Flip_Flop j_k_ff_2 (
    .J(or_2_out), .clk(Clock), .K(or_2_out), .Q(A2), .Qn(j_k_ff_2_qn), .reset(or_6_out));  // open: preset, en
  or or_6 (or_6_out, or_5_out, Preset_out);
  J_K_Flip_Flop j_k_ff_3 (
    .J(or_3_out), .clk(Clock), .K(or_3_out), .Q(A3), .Qn(j_k_ff_3_qn), .reset(or_7_out));  // open: preset, en
  or or_7 (or_7_out, or_5_out, Preset_out);
  J_K_Flip_Flop j_k_ff_4 (
    .J(or_4_out), .clk(Clock), .K(or_4_out), .Q(A4_MSB), .preset(Preset_out), .reset(or_5_out));  // open: Qn, en
  and u_Clear (Clear_out, Clock, j_k_ff_3_qn, A2, j_k_ff_1_qn, A4_MSB);
  and Preset (Preset_out, Clock, A1_lsb, A2, A3, A4_MSB);
  Hex_Digit_Display hex_digit_display_1 (.value({A4_MSB, A3, A2, A1_lsb}), .dp(1'b0));

  assign HEX = {A4_MSB, A3, A2, A1_lsb};
endmodule

module cascade_decade_counter (
  input  Up1_down0,
  input  Clear
);

  wire clock_1_out, main_1_a4_msb, multiplexer_1_out, not_1_out;
  wire [3:0] main_1_hex, main_2_hex;

  Clock clock_1 (.out(clock_1_out));
  main main_1 (
    .Up1_down0(Up1_down0), .Clear(Clear), .Clock(clock_1_out), .HEX(main_1_hex), .A4_MSB(main_1_a4_msb));  // open: A1_lsb, A2, A3
  not not_1 (not_1_out, main_1_a4_msb);
  Multiplexer multiplexer_1 (
    .in0(main_1_a4_msb), .in1(not_1_out), .out(multiplexer_1_out), .sel(Up1_down0));  // open: en
  Hex_Digit_Display hex_digit_display_1 (.value(main_2_hex));  // open: dp
  Hex_Digit_Display hex_digit_display_2 (.value(main_1_hex));  // open: dp
  main main_2 (
    .Up1_down0(Up1_down0), .Clear(Clear), .Clock(multiplexer_1_out), .HEX(main_2_hex));  // open: A1_lsb, A2, A3, A4_MSB
endmodule

module bcd_to_7_segment (
  input  A_MSB,
  input  B,
  input  C,
  input  D_LSB,
  output A,
  output B_2,
  output C_2,
  output D,
  output E,
  output F,
  output G
);

  wire B_prime_C_out, B_prime_D_prime_out, BC_prime_out, BD_out, BD_prime_out, C_prime_D_prime_out, CD_out,
       CD_prime_out, not_1_out, not_2_out, not_3_out, not_4_out, xor_1_out;

  not not_1 (not_1_out, A_MSB);
  not not_2 (not_2_out, B);
  not not_3 (not_3_out, C);
  not not_4 (not_4_out, D_LSB);
  and BD (BD_out, B, D_LSB);
  and B_prime_D_prime (B_prime_D_prime_out, not_2_out, not_4_out);
  and CD (CD_out, C, D_LSB);
  and C_prime_D_prime (C_prime_D_prime_out, not_3_out, not_4_out);
  and CD_prime (CD_prime_out, C, not_4_out);
  and BC_prime (BC_prime_out, B, not_3_out);
  and BD_prime (BD_prime_out, B, not_4_out);
  and B_prime_C (B_prime_C_out, not_2_out, C);
  xor xor_1 (xor_1_out, BD_out, C);
  or u_A (A, BD_out, A_MSB, B_prime_D_prime_out, C);
  or u_B (B_2, CD_out, not_2_out, C_prime_D_prime_out);
  or u_C (C_2, B, not_3_out, D_LSB);
  or u_D (D, xor_1_out, A_MSB, B_prime_D_prime_out);
  or u_E (E, CD_prime_out, B_prime_D_prime_out);
  or u_F (F, BC_prime_out, A_MSB, C_prime_D_prime_out, BD_prime_out);
  or u_G (G, A_MSB, BC_prime_out, CD_prime_out, B_prime_C_out);
  _7_Segment_Display u_7_segment_display_1 (.g(G), .f(F), .a(A), .b(B_2), .e(E), .d(D), .c(C_2));  // open: dp
endmodule

module decade_counter (
  input  UP1_down0,
  input  CLEAR
);

  wire bcd_to_7_segment_1_a, bcd_to_7_segment_1_b_2, bcd_to_7_segment_1_c_2, bcd_to_7_segment_1_d,
       bcd_to_7_segment_1_e, bcd_to_7_segment_1_f, bcd_to_7_segment_1_g, cLOCK_out, main_1_a1_lsb, main_1_a2,
       main_1_a3, main_1_a4_msb;

  Clock cLOCK (.out(cLOCK_out));
  main main_1 (
    .Up1_down0(UP1_down0), .Clear(CLEAR), .Clock(cLOCK_out), .A1_lsb(main_1_a1_lsb), .A2(main_1_a2),
    .A3(main_1_a3), .A4_MSB(main_1_a4_msb));  // open: HEX
  bcd_to_7_segment bcd_to_7_segment_1 (
    .A_MSB(main_1_a4_msb), .B(main_1_a3), .C(main_1_a2), .D_LSB(main_1_a1_lsb), .A(bcd_to_7_segment_1_a),
    .B_2(bcd_to_7_segment_1_b_2), .C_2(bcd_to_7_segment_1_c_2), .D(bcd_to_7_segment_1_d),
    .E(bcd_to_7_segment_1_e), .F(bcd_to_7_segment_1_f), .G(bcd_to_7_segment_1_g));
  _7_Segment_Display u_7_segment_display_1 (
    .g(bcd_to_7_segment_1_g), .f(bcd_to_7_segment_1_f), .a(bcd_to_7_segment_1_a), .b(bcd_to_7_segment_1_b_2),
    .e(bcd_to_7_segment_1_e), .d(bcd_to_7_segment_1_d), .c(bcd_to_7_segment_1_c_2));  // open: dp
endmodule

module cascade_2 (
  input  Up1_down0,
  input  Clear
);

  wire clock_1_out, DOWN_out, main_1_a1_lsb, main_1_a2, main_1_a3, main_1_a4_msb, multiplexer_1_out,
       not_1_out, not_2_out, UP_out;
  wire [3:0] main_1_hex, main_2_hex;

  Clock clock_1 (.out(clock_1_out));
  main main_1 (
    .Up1_down0(Up1_down0), .Clear(Clear), .Clock(clock_1_out), .A1_lsb(main_1_a1_lsb), .HEX(main_1_hex),
    .A2(main_1_a2), .A3(main_1_a3), .A4_MSB(main_1_a4_msb));
  not not_1 (not_1_out, main_1_a1_lsb);
  not not_2 (not_2_out, main_1_a4_msb);
  or DOWN (DOWN_out, main_1_a1_lsb, main_1_a2, main_1_a3, main_1_a4_msb);
  or UP (UP_out, main_1_a2, main_1_a2, not_1_out, not_2_out);
  Multiplexer multiplexer_1 (.in0(DOWN_out), .in1(UP_out), .out(multiplexer_1_out), .sel(Up1_down0));  // open: en
  main main_2 (
    .Up1_down0(Up1_down0), .Clear(Clear), .Clock(multiplexer_1_out), .HEX(main_2_hex));  // open: A1_lsb, A2, A3, A4_MSB
  Hex_Digit_Display hex_digit_display_1 (.value(main_1_hex));  // open: dp
  Hex_Digit_Display hex_digit_display_2 (.value(main_2_hex));  // open: dp
endmodule
