// Logisim project Traffic Sysytem.circ as structural Verilog: 16 circuits, main circuit main
module main (
  input  Clear,
  input  Count
);

  wire clock_1_out, mod_60_counter_1_next_clock, traffic_board_1_right_turn__ew,
       traffic_board_1_right_turn_ns, traffic_board_1_straight_ew, traffic_board_1_straight_ns;
  wire [1:0] Mod_4_out_4;
  wire [3:0] mod_60_counter_1_lsb, mod_60_counter_1_msb;

  _24H_Clock u_24h_clock_1 ();  // open: Lpad, Count, Clock, Clear, H_msb, H_lsb, M_msb, M_lsb, S_msb, S_lsb, in_9, in_10, in_7, in_8, in_5, in_6
  Clock clock_1 (.out(clock_1_out));
  Hex_Digit_Display hex_digit_display_1 (.value(mod_60_counter_1_msb));  // open: dp
  Hex_Digit_Display hex_digit_display_2 (.value(mod_60_counter_1_lsb));  // open: dp
  Mod_60_counter mod_60_counter_1 (
    .Clock(clock_1_out), .Clear(Clear), .MSB(mod_60_counter_1_msb), .LSB(mod_60_counter_1_lsb),
    .Next_Clock(mod_60_counter_1_next_clock));
  Mod_4_Up_Counter Mod_4 (.Count(Count), .Clock(mod_60_counter_1_next_clock), .Clear(Clear), .out_4(Mod_4_out_4));
  LED Right_Turn (.in(traffic_board_1_right_turn__ew));
  LED RED_gREEN (.in(traffic_board_1_straight_ew));
  LED RED_gREEN_2 (.in(traffic_board_1_straight_ns));
  Traffic_Board traffic_board_1 (
    .Input(Mod_4_out_4), .Straight_NS(traffic_board_1_straight_ns),
    .Right_Turn_NS(traffic_board_1_right_turn_ns), .Right_Turn__EW(traffic_board_1_right_turn__ew),
    .Straight_EW(traffic_board_1_straight_ew));
  LED RED_gREEN_3 (.in(traffic_board_1_straight_ns));
  LED Right_Turn_2 (.in(traffic_board_1_right_turn_ns));
  LED Right_Turn_3 (.in(traffic_board_1_right_turn_ns));
  LED Right_Turn_4 (.in(traffic_board_1_right_turn__ew));
  LED RED_gREEN_4 (.in(traffic_board_1_straight_ew));
endmodule

module Traffic_Board (
  input  [1:0] Input,
  output Straight_NS,
  output Right_Turn_NS,
  output Right_Turn__EW,
  output Straight_EW
);

  wire not_1_out, not_2_out;

  not not_1 (not_1_out, Input[1]);
  not not_2 (not_2_out, Input[0]);
  and I1I2_prime (Straight_EW, not_2_out, Input[1]);
  and I1I2 (Right_Turn__EW, Input[0], Input[1]);
  and I1_prime_I2_prime (Straight_NS, not_2_out, not_1_out);
  and I1_prime_I2 (Right_Turn_NS, Input[0], not_1_out);
  LED Right_Turn (.in(Right_Turn__EW));
  LED RED_gREEN (.in(Straight_EW));
  LED RED_gREEN_2 (.in(Straight_NS));
  LED RED_gREEN_3 (.in(Straight_NS));
  LED Right_Turn_2 (.in(Right_Turn_NS));
  LED Right_Turn_3 (.in(Right_Turn_NS));
  LED Right_Turn_4 (.in(Right_Turn__EW));
  LED RED_gREEN_4 (.in(Straight_EW));
endmodule

module Mod_4_Up_Counter (
  input  Count,
  input  Clock,
  input  Clear,
  output [1:0] out_4
);

  wire and_1_out;

  J_K_Flip_Flop j_k_ff_1 (.J(Count), .clk(Clock), .K(Count), .Q(out_4[0]), .reset(Clear));  // open: Qn, preset, en
  and and_1 (and_1_out, out_4[0], Count);
  J_K_Flip_Flop j_k_ff_2 (
    .J(and_1_out), .clk(Clock), .K(and_1_out), .Q(out_4[1]), .reset(Clear));  // open: Qn, preset, en
endmodule

module decade_Up_down_Counter (
  input  Up1_down0,
  input  Clear,
  input  Clock,
  output A1_lsb,
  output [3:0] HEX,
  output A2,
  output A3,
  output A4_MSB
);

  wire and_1_out, and_2_out, and_3_out, and_4_out, and_5_out, and_6_out, Clear_out, j_k_ff_1_qn, j_k_ff_2_qn,
       j_k_ff_3_qn, not_1_out, or_1_out, or_2_out, or_3_out, or_4_out, or_5_out, or_6_out, or_7_out,
       Preset_out;

  not not_1 (not_1_out, Up1_down0);
  and and_1 (and_1_out, j_k_ff_1_qn, not_1_out);
  and and_2 (and_2_out, A1_lsb, Up1_down0);
  and and_3 (and_3_out, j_k_ff_2_qn, and_1_out);
  and and_4 (and_4_out, j_k_ff_3_qn, and_3_out);
  and and_5 (and_5_out, A3, and_6_out);
  or or_1 (or_1_out, Up1_down0, not_1_out);
  or or_2 (or_2_out, and_2_out, and_1_out);
  and and_6 (and_6_out, and_2_out, A2);
  or or_3 (or_3_out, and_6_out, and_3_out);
  or or_4 (or_4_out, and_5_out, and_4_out);
  or or_5 (or_5_out, Clear_out, Clear);
  J_K_Flip_Flop j_k_ff_1 (
    .J(or_1_out), .clk(Clock), .K(or_1_out), .Q(A1_lsb), .Qn(j_k_ff_1_qn), .preset(Preset_out),
    .reset(or_5_out));  // open: en
  J_K_Flip_Flop j_k_ff_2 (
    .J(or_2_out), .clk(Clock), .K(or_2_out), .Q(A2), .Qn(j_k_ff_2_qn), .reset(or_6_out));  // open: preset, en
  or or_6 (or_6_out, or_5_out, Preset_out);
  J_K_Flip_Flop j_k_ff_3 (
    .J(or_3_out), .clk(Clock), .K(or_3_out), .Q(A3), .Qn(j_k_ff_3_qn), .reset(or_7_out));  // open: preset, en
  or or_7 (or_7_out, or_5_out, Preset_out);
  J_K_Flip_Flop j_k_ff_4 (
    .J(or_4_out), .clk(Clock), .K(or_4_out), .Q(A4_MSB), .preset(Preset_out), .reset(or_5_out));  // open: Qn, en
  and u_Clear (Clear_out, Clock, j_k_ff_3_qn, A2, j_k_ff_1_qn, A4_MSB);
  and Preset (Preset_out, Clock, A1_lsb, A2, A3, A4_MSB);
  Hex_Digit_Display hex_digit_display_1 (.value({A4_MSB, A3, A2, A1_lsb}), .dp(1'b0));

  assign HEX = {A4_MSB, A3, A2, A1_lsb};
endmodule

module Mod_60_counter (
  input  Clock,
  input  Clear,
  output [3:0] MSB,
  output [3:0] LSB,
  output Next_Clock
);

  wire _5_prime_out, _9_prime_out, clock_1_out, decade_up_down_counter_1_a1_lsb, decade_up_down_counter_1_a2,
       decade_up_down_counter_1_a3, decade_up_down_counter_1_a4_msb, not_1_out, not_2_out, not_3_out,
       not_4_out, not_5_out, nUP_out;

  Clock clock_1 (.out(clock_1_out));
  not nUP (nUP_out, 1'b0);
  nand nand_1 (Next_Clock, _9_prime_out, _5_prime_out);
  decade_Up_down_Counter decade_up_down_counter_1 (
    .Up1_down0(nUP_out), .Clear(Clear), .Clock(Clock), .A1_lsb(decade_up_down_counter_1_a1_lsb), .HEX(LSB),
    .A2(decade_up_down_counter_1_a2), .A3(decade_up_down_counter_1_a3),
    .A4_MSB(decade_up_down_counter_1_a4_msb));
  and _9_prime (_9_prime_out, decade_up_down_counter_1_a4_msb, not_2_out, not_3_out, decade_up_down_counter_1_a1_lsb);
  not not_1 (not_1_out, decade_up_down_counter_1_a4_msb);
  not not_2 (not_2_out, decade_up_down_counter_1_a3);
  not not_3 (not_3_out, decade_up_down_counter_1_a2);
  and _5_prime (_5_prime_out, not_4_out, not_5_out, MSB[0], MSB[2]);
  not not_4 (not_4_out, MSB[1]);
  mod_6_Counter_up mod_6_counter_up_1 (.Count(nUP_out), .Clock(not_1_out), .Clear(Clear), .Hex(MSB));
  not not_5 (not_5_out, MSB[3]);
  Hex_Digit_Display hex_digit_display_1 (.value(MSB));  // open: dp
  Hex_Digit_Display hex_digit_display_2 (.value(LSB));  // open: dp
endmodule

module mod_6_Counter_up (
  input  Count,
  input  Clock,
  input  Clear,
  output [3:0] Hex
);

  wire and_1_out, and_2_out, and_3_out, j_k_ff_1_qn, or_1_out;

  and and_1 (and_1_out, Count, Hex[0]);
  and and_2 (and_2_out, and_1_out, Hex[1]);
  or or_1 (or_1_out, Clear, and_3_out);
  and and_3 (and_3_out, j_k_ff_1_qn, Hex[1], Hex[2]);
  J_K_Flip_Flop j_k_ff_1 (
    .J(Count), .clk(Clock), .K(Count), .Q(Hex[0]), .Qn(j_k_ff_1_qn), .reset(or_1_out));  // open: preset, en
  J_K_Flip_Flop j_k_ff_2 (
    .J(and_1_out), .clk(Clock), .K(and_1_out), .Q(Hex[1]), .reset(or_1_out));  // open: Qn, preset, en
  J_K_Flip_Flop j_k_ff_3 (
    .J(and_2_out), .clk(Clock), .K(and_2_out), .Q(Hex[2]), .reset(or_1_out));  // open: Qn, preset, en
  Hex_Digit_Display hex_digit_display_1 (.value({1'b0, Hex[2:0]}));  // open: dp

  assign Hex[3] = 1'b0;
endmodule

module Mod_30_counter (
  input  Clock,
  input  Clear,
  output [3:0] MSB,
  output [3:0] LSB,
  output Next_Clock
);

  wire _2_prime_out, _9_prime_out, clock_1_out, decade_up_down_counter_1_a1_lsb, decade_up_down_counter_1_a2,
       decade_up_down_counter_1_a3, decade_up_down_counter_1_a4_msb, not_1_out, not_2_out, not_3_out,
       not_4_out, not_5_out, not_6_out, nUP_out;

  Clock clock_1 (.out(clock_1_out));
  not nUP (nUP_out, 1'b0);
  nand nand_1 (Next_Clock, _9_prime_out, _2_prime_out);
  decade_Up_down_Counter decade_up_down_counter_1 (
    .Up1_down0(nUP_out), .Clear(Clear), .Clock(Clock), .A1_lsb(decade_up_down_counter_1_a1_lsb), .HEX(LSB),
    .A2(decade_up_down_counter_1_a2), .A3(decade_up_down_counter_1_a3),
    .A4_MSB(decade_up_down_counter_1_a4_msb));
  and _9_prime (_9_prime_out, decade_up_down_counter_1_a4_msb, not_1_out, not_2_out, decade_up_down_counter_1_a1_lsb);
  not not_1 (not_1_out, decade_up_down_counter_1_a3);
  not not_2 (not_2_out, decade_up_down_counter_1_a2);
  not not_3 (not_3_out, decade_up_down_counter_1_a4_msb);
  and _2_prime (_2_prime_out, not_4_out, not_5_out, MSB[1], not_6_out);
  not not_4 (not_4_out, 1'b0);
  mod_3_counter mod_3_counter_1 (.Count(nUP_out), .Clock(not_3_out), .Clear(Clear), .out_4(MSB[1:0]));
  not not_5 (not_5_out, MSB[0]);
  not not_6 (not_6_out, 1'b0);
  Hex_Digit_Display hex_digit_display_1 (.value({2'b00, MSB[1:0]}));  // open: dp
  Hex_Digit_Display hex_digit_display_2 (.value(LSB));  // open: dp

  assign MSB[3:2] = 2'b00;
endmodule

module mod_3_counter (
  input  Count,
  input  Clock,
  input  Clear,
  output [1:0] out_4
);

  wire and_1_out, and_2_out, or_1_out;

  J_K_Flip_Flop j_k_ff_1 (.J(Count), .clk(Clock), .K(Count), .Q(out_4[0]), .reset(or_1_out));  // open: Qn, preset, en
  or or_1 (or_1_out, Clear, and_2_out);
  and and_1 (and_1_out, out_4[0], Count);
  J_K_Flip_Flop j_k_ff_2 (
    .J(and_1_out), .clk(Clock), .K(and_1_out), .Q(out_4[1]), .reset(or_1_out));  // open: Qn, preset, en
  and and_2 (and_2_out, out_4[1], out_4[0]);
endmodule

module comparator (
  input  [3:0] A,
  input  [3:0] B,
  output A_B,
  output A_B_2,
  output A__B
);

  wire and_1_out, and_2_out, and_3_out, and_4_out, and_5_out, and_6_out, and_7_out, and_8_out, and_9_out,
       and_10_out, and_11_out, and_12_out, and_13_out, and_14_out, nor_1_out, nor_2_out, nor_3_out,
       nor_4_out, not_1_out, not_2_out, not_3_out, not_4_out, not_5_out, not_6_out, not_7_out, not_8_out;

  not not_1 (not_1_out, A[3]);
  not not_2 (not_2_out, B[3]);
  not not_3 (not_3_out, A[2]);
  not not_4 (not_4_out, B[2]);
  not not_5 (not_5_out, A[1]);
  not not_6 (not_6_out, B[1]);
  not not_7 (not_7_out, A[0]);
  not not_8 (not_8_out, B[0]);
  and and_1 (and_1_out, not_1_out, B[3]);
  and and_2 (and_2_out, A[3], not_2_out);
  and and_3 (and_3_out, not_3_out, B[2]);
  and and_4 (and_4_out, A[2], not_4_out);
  and and_5 (and_5_out, not_5_out, B[1]);
  and and_6 (and_6_out, A[1], not_6_out);
  and and_7 (and_7_out, not_7_out, B[0]);
  and and_8 (and_8_out, A[0], not_8_out);
  nor nor_1 (nor_1_out, and_1_out, and_2_out);
  nor nor_2 (nor_2_out, and_3_out, and_4_out);
  nor nor_3 (nor_3_out, and_5_out, and_6_out);
  nor nor_4 (nor_4_out, and_7_out, and_8_out);
  and and_9 (and_9_out, nor_1_out, and_3_out);
  and and_10 (and_10_out, nor_1_out, and_4_out);
  and and_11 (and_11_out, nor_1_out, nor_2_out, and_5_out);
  and and_12 (and_12_out, nor_1_out, nor_2_out, and_6_out);
  and and_13 (and_13_out, nor_1_out, nor_2_out, nor_3_out, and_7_out);
  and and_14 (and_14_out, nor_1_out, nor_2_out, nor_3_out, and_8_out);
  and and_15 (A__B, nor_1_out, nor_2_out, nor_3_out, nor_4_out);
  or or_1 (A_B, and_1_out, and_9_out, and_11_out, and_13_out);
  or or_2 (A_B_2, and_2_out, and_10_out, and_12_out, and_14_out);
endmodule

module Extra_Logic_Board (
  input  [3:0] H_msb,
  input  [3:0] H_lsb,
  output Busy_Time
);

  wire and_1_out, and_2_out, and_3_out, and_4_out, L_2_a__b, L_3_a__b, L_4_a__b, L_a__b, M_2_a__b, M_3_a__b,
       M_4_a__b, M_a__b;
  wire [3:3] not_1_out;

  not not_1 (not_1_out[3], 1'b0);
  comparator M (.A(H_msb), .B(4'b0000), .A__B(M_a__b));  // open: A_B, A_B_2
  comparator L (.A(H_lsb), .B({not_1_out[3], 2'b00, not_1_out[3]}), .A__B(L_a__b));  // open: A_B, A_B_2
  comparator M_2 (.A(H_msb), .B({3'b000, not_1_out[3]}), .A__B(M_2_a__b));  // open: A_B, A_B_2
  comparator L_2 (.A(H_lsb), .B(4'b0000), .A__B(L_2_a__b));  // open: A_B, A_B_2
  comparator M_3 (.A(H_msb), .B({3'b000, not_1_out[3]}), .A__B(M_3_a__b));  // open: A_B, A_B_2
  comparator L_3 (.A(H_lsb), .B({1'b0, {3{not_1_out[3]}}}), .A__B(L_3_a__b));  // open: A_B, A_B_2
  comparator M_4 (.A(H_msb), .B({3'b000, not_1_out[3]}), .A__B(M_4_a__b));  // open: A_B, A_B_2
  comparator L_4 (.A(H_lsb), .B({not_1_out[3], 3'b000}), .A__B(L_4_a__b));  // open: A_B, A_B_2
  and and_1 (and_1_out, M_2_a__b, L_2_a__b);
  and and_2 (and_2_out, M_a__b, L_a__b);
  and and_3 (and_3_out, M_3_a__b, L_3_a__b);
  and and_4 (and_4_out, M_4_a__b, L_4_a__b);
  or or_1 (Busy_Time, and_2_out, and_1_out, and_3_out, and_4_out);
endmodule

module decade_counter_loaded (
  input  Count,
  input  Load,
  input  [3:0] Load_Value,
  input  Clock,
  input  Clear,
  output [3:0] out_6,
  output A0,
  output A1,
  output A2,
  output A3
);

  wire _0_qn, _2_qn, and_1_out, and_2_out, and_3_out, and_4_out, and_5_out, and_6_out, and_7_out, and_8_out,
       and_9_out, and_10_out, and_11_out, and_12_out, and_13_out, not_1_out, not_2_out, not_3_out, not_4_out,
       not_5_out, or_1_out, or_2_out, or_3_out, or_4_out, or_5_out, or_6_out, or_7_out, or_8_out, or_9_out;

  not not_1 (not_1_out, Load);
  not not_2 (not_2_out, Load_Value[3]);
  and and_1 (and_1_out, Count, not_1_out);
  not not_3 (not_3_out, Load_Value[0]);
  not not_4 (not_4_out, Load_Value[1]);
  not not_5 (not_5_out, Load_Value[2]);
  and and_2 (and_2_out, Load, Load_Value[0]);
  and and_3 (and_3_out, Load, not_3_out);
  and and_4 (and_4_out, Load_Value[1], Load);
  and and_5 (and_5_out, not_4_out, Load);
  and and_6 (and_6_out, Load_Value[2], Load);
  and and_7 (and_7_out, Load, not_5_out);
  and and_8 (and_8_out, Load_Value[3], Load);
  and and_9 (and_9_out, Load, not_2_out);
  or or_1 (or_1_out, Clear, and_13_out);
  and and_10 (and_10_out, and_1_out, A0);
  and and_11 (and_11_out, and_1_out, A0, A1);
  and and_12 (and_12_out, and_1_out, A0, A1, A2);
  or or_2 (or_2_out, and_2_out, and_1_out);
  or or_3 (or_3_out, and_3_out, and_1_out);
  or or_4 (or_4_out, and_4_out, and_10_out);
  or or_5 (or_5_out, and_10_out, and_5_out);
  or or_6 (or_6_out, and_6_out, and_11_out);
  or or_7 (or_7_out, and_11_out, and_7_out);
  or or_8 (or_8_out, and_8_out, and_12_out);
  or or_9 (or_9_out, and_12_out, and_9_out);
  J_K_Flip_Flop _0 (.J(or_2_out), .clk(Clock), .K(or_3_out), .Q(A0), .Qn(_0_qn), .reset(or_1_out));  // open: preset, en
  and and_13 (and_13_out, A3, _2_qn, A1, _0_qn);
  J_K_Flip_Flop _1 (.J(or_4_out), .clk(Clock), .K(or_5_out), .Q(A1), .reset(or_1_out));  // open: Qn, preset, en
  J_K_Flip_Flop _2 (.J(or_6_out), .clk(Clock), .K(or_7_out), .Q(A2), .Qn(_2_qn), .reset(or_1_out));  // open: preset, en
  J_K_Flip_Flop _3 (.J(or_8_out), .clk(Clock), .K(or_9_out), .Q(A3), .reset(or_1_out));  // open: Qn, preset, en
  Hex_Digit_Display hex_digit_display_1 (.value({A3, A2, A1, A0}));  // open: dp

  assign out_6 = {A3, A2, A1, A0};
endmodule

module _0_59_Counter_loaded (
  input  [3:0] Load_Ten_s_Place,
  input  [3:0] Load_One_s_Place,
  input  Load,
  input  Count,
  input  Clock,
  input  Clear,
  output [3:0] MSB,
  output [3:0] LSB,
  output Next_Clock
);

  wire _0_prime_out, _6_prime_2_out, _6_prime_out, and_1_out, and_2_out, decade_counter_loaded_1_a0,
       decade_counter_loaded_1_a1, decade_counter_loaded_1_a2, decade_counter_loaded_1_a3,
       decade_counter_loaded_2_a0, decade_counter_loaded_2_a1, decade_counter_loaded_2_a2,
       decade_counter_loaded_2_a3, not_1_out, not_2_out, not_3_out, not_4_out, not_5_out, not_6_out,
       not_7_out, or_1_out;

  or or_1 (or_1_out, Clear, and_1_out);
  and and_1 (and_1_out, _0_prime_out, _6_prime_out);
  decade_counter_loaded decade_counter_loaded_1 (
    .Count(Count), .Load(Load), .Load_Value(Load_One_s_Place), .Clock(Clock), .Clear(or_1_out), .out_6(LSB),
    .A0(decade_counter_loaded_1_a0), .A1(decade_counter_loaded_1_a1), .A2(decade_counter_loaded_1_a2),
    .A3(decade_counter_loaded_1_a3));
  and _0_prime (_0_prime_out, not_1_out, not_2_out, not_3_out, not_4_out);
  not not_1 (not_1_out, decade_counter_loaded_1_a3);
  not not_2 (not_2_out, decade_counter_loaded_1_a2);
  not not_3 (not_3_out, decade_counter_loaded_1_a1);
  not not_4 (not_4_out, decade_counter_loaded_1_a0);
  and _6_prime (_6_prime_out, not_5_out, decade_counter_loaded_2_a2, decade_counter_loaded_2_a1, not_6_out);
  and and_2 (and_2_out, decade_counter_loaded_1_a3, not_3_out, Count, not_2_out, decade_counter_loaded_1_a0);
  not not_5 (not_5_out, decade_counter_loaded_2_a3);
  not not_6 (not_6_out, decade_counter_loaded_2_a0);
  decade_counter_loaded decade_counter_loaded_2 (
    .Count(and_2_out), .Load(Load), .Load_Value(Load_Ten_s_Place), .Clock(Clock), .Clear(or_1_out),
    .out_6(MSB), .A0(decade_counter_loaded_2_a0), .A1(decade_counter_loaded_2_a1),
    .A2(decade_counter_loaded_2_a2), .A3(decade_counter_loaded_2_a3));
  Hex_Digit_Display hex_digit_display_1 (.value(LSB));  // open: dp
  Hex_Digit_Display hex_digit_display_2 (.value(MSB));  // open: dp
  not not_7 (not_7_out, decade_counter_loaded_2_a1);
  and _6_prime_2 (_6_prime_2_out, decade_counter_loaded_2_a0, not_7_out, decade_counter_loaded_2_a2, not_5_out);
  and and_3 (Next_Clock, and_2_out, Count, _6_prime_2_out);
endmodule

module mod_3_Counter_Loaded (
  input  Count,
  input  Load,
  input  [1:0] Load_Value,
  input  Clock,
  input  Clear,
  output [3:0] Hex,
  output A0,
  output A1,
  output A2,
  output A3
);

  wire and_1_out, and_2_out, and_3_out, and_4_out, and_5_out, and_6_out, and_7_out, not_1_out, not_2_out,
       not_3_out, or_1_out, or_2_out, or_3_out, or_4_out, or_5_out;

  not not_1 (not_1_out, Load);
  and and_1 (and_1_out, Count, not_1_out);
  not not_2 (not_2_out, Load_Value[0]);
  not not_3 (not_3_out, Load_Value[1]);
  and and_2 (and_2_out, Load, Load_Value[0]);
  and and_3 (and_3_out, Load, not_2_out);
  and and_4 (and_4_out, Load_Value[1], Load);
  and and_5 (and_5_out, not_3_out, Load);
  or or_1 (or_1_out, Clear, and_7_out);
  and and_6 (and_6_out, and_1_out, A0);
  or or_2 (or_2_out, and_2_out, and_1_out);
  or or_3 (or_3_out, and_3_out, and_1_out);
  or or_4 (or_4_out, and_4_out, and_6_out);
  or or_5 (or_5_out, and_6_out, and_5_out);
  J_K_Flip_Flop _0 (.J(or_2_out), .clk(Clock), .K(or_3_out), .Q(A0), .reset(or_1_out));  // open: Qn, preset, en
  and and_7 (and_7_out, A1, A0);
  J_K_Flip_Flop _1 (.J(or_4_out), .clk(Clock), .K(or_5_out), .Q(A1), .reset(or_1_out));  // open: Qn, preset, en
  Hex_Digit_Display hex_digit_display_1 (.value({2'b00, A1, A0}));  // open: dp

  assign A2 = 1'b0;
  assign A3 = 1'b0;
  assign Hex = {2'b00, A1, A0};
endmodule

module _0_23_Counter_Loaded (
  input  [1:0] Load_ten_s_Place,
  input  [3:0] Load_one_s_Place,
  input  Load,
  input  Count,
  input  Clock,
  input  Clear,
  output [3:0] MSB,
  output [3:0] LSB
);

  wire _4_prime_2_out, _4_prime_out, and_1_out, and_2_out, decade_counter_loaded_1_a0,
       decade_counter_loaded_1_a1, decade_counter_loaded_1_a2, decade_counter_loaded_1_a3,
       mod_3_counter_loaded_1_a0, mod_3_counter_loaded_1_a1, mod_3_counter_loaded_1_a2,
       mod_3_counter_loaded_1_a3, not_1_out, not_2_out, not_3_out, not_4_out, not_5_out, not_6_out,
       not_7_out, or_1_out;

  or or_1 (or_1_out, Clear, and_1_out);
  and and_1 (and_1_out, _4_prime_out, _4_prime_2_out);
  decade_counter_loaded decade_counter_loaded_1 (
    .Count(Count), .Load(Load), .Load_Value(Load_one_s_Place), .Clock(Clock), .Clear(or_1_out), .out_6(LSB),
    .A0(decade_counter_loaded_1_a0), .A1(decade_counter_loaded_1_a1), .A2(decade_counter_loaded_1_a2),
    .A3(decade_counter_loaded_1_a3));
  and _4_prime (_4_prime_out, not_1_out, decade_counter_loaded_1_a2, not_2_out, not_3_out);
  not not_1 (not_1_out, decade_counter_loaded_1_a3);
  not not_2 (not_2_out, decade_counter_loaded_1_a1);
  not not_3 (not_3_out, decade_counter_loaded_1_a0);
  and _4_prime_2 (_4_prime_2_out, not_5_out, not_6_out, mod_3_counter_loaded_1_a1, not_7_out);
  not not_4 (not_4_out, decade_counter_loaded_1_a2);
  not not_5 (not_5_out, mod_3_counter_loaded_1_a3);
  and and_2 (and_2_out, decade_counter_loaded_1_a3, not_4_out, Count, decade_counter_loaded_1_a0, not_2_out);
  not not_6 (not_6_out, mod_3_counter_loaded_1_a2);
  not not_7 (not_7_out, mod_3_counter_loaded_1_a0);
  mod_3_Counter_Loaded mod_3_counter_loaded_1 (
    .Count(and_2_out), .Load(Load), .Load_Value(Load_ten_s_Place), .Clock(Clock), .Clear(or_1_out),
    .Hex(MSB), .A0(mod_3_counter_loaded_1_a0), .A1(mod_3_counter_loaded_1_a1),
    .A2(mod_3_counter_loaded_1_a2), .A3(mod_3_counter_loaded_1_a3));
  Hex_Digit_Display hex_digit_display_1 (.value(MSB));  // open: dp
  Hex_Digit_Display hex_digit_display_2 (.value(LSB));  // open: dp
endmodule

module _24H_Clock (
  input  Lpad,
  input  Count,
  input  Clock,
  input  Clear,
  input  [3:0] in_5,
  input  [3:0] in_6,
  input  [3:0] in_7,
  input  [3:0] in_8,
  input  [1:0] in_9,
  input  [3:0] in_10,
  output [3:0] M_msb,
  output [3:0] M_lsb,
  output [3:0] S_msb,
  output [3:0] S_lsb,
  output [3:0] H_msb,
  output [3:0] H_lsb
);

  wire n0_59_counter_loaded_1_next_clock, n0_59_counter_loaded_2_next_clock;

  Hex_Digit_Display hex_digit_display_1 (.value(H_msb));  // open: dp
  _0_23_Counter_Loaded u_0_23_counter_loaded_1 (
    .Load_ten_s_Place(in_9), .Load_one_s_Place(in_10), .Load(Lpad),
    .Count(n0_59_counter_loaded_1_next_clock), .Clock(Clock), .Clear(Clear), .MSB(H_msb), .LSB(H_lsb));
  Hex_Digit_Display hex_digit_display_2 (.value(H_lsb));  // open: dp
  Hex_Digit_Display hex_digit_display_3 (.value(M_msb));  // open: dp
  Hex_Digit_Display hex_digit_display_4 (.value(M_lsb));  // open: dp
  _0_59_Counter_loaded u_0_59_counter_loaded_1 (
    .Load_Ten_s_Place(in_7), .Load_One_s_Place(in_8), .Load(Lpad), .Count(n0_59_counter_loaded_2_next_clock),
    .Clock(Clock), .Clear(Clear), .MSB(M_msb), .LSB(M_lsb), .Next_Clock(n0_59_counter_loaded_1_next_clock));
  Hex_Digit_Display hex_digit_display_5 (.value(S_msb));  // open: dp
  Hex_Digit_Display hex_digit_display_6 (.value(S_lsb));  // open: dp
  _0_59_Counter_loaded u_0_59_counter_loaded_2 (
    .Load_Ten_s_Place(in_5), .Load_One_s_Place(in_6), .Load(Lpad), .Count(Count), .Clock(Clock),
    .Clear(Clear), .MSB(S_msb), .LSB(S_lsb), .Next_Clock(n0_59_counter_loaded_2_next_clock));
endmodule

module Traffic__System (
  input  Load,
  input  Count,
  input  Clear,
  input  [1:0] in_4,
  input  [3:0] in_5,
  input  [3:0] in_6,
  input  [3:0] in_7,
  input  [3:0] in_8,
  input  [3:0] in_9
);

  wire _30_next_clock, _60_next_clock, and_1_out, Busy_Time_busy_time, clock_1_out, demultiplexer_1_out0,
       demultiplexer_1_out1, not_1_out, traffic_board_1_right_turn__ew, traffic_board_1_right_turn_ns,
       traffic_board_1_straight_ew, traffic_board_1_straight_ns;
  wire [1:0] Mod_4_out_4;
  wire [3:0] _30_lsb, _30_msb, _60_lsb, _60_msb, n24h_clock_1_h_lsb, n24h_clock_1_h_msb, n24h_clock_1_m_lsb,
       n24h_clock_1_m_msb, n24h_clock_1_s_lsb, n24h_clock_1_s_msb;

  Hex_Digit_Display hex_digit_display_1 (.value(n24h_clock_1_h_msb));  // open: dp
  Clock clock_1 (.out(clock_1_out));
  Hex_Digit_Display hex_digit_display_2 (.value(n24h_clock_1_m_msb));  // open: dp
  Hex_Digit_Display hex_digit_display_3 (.value(n24h_clock_1_h_lsb));  // open: dp
  Hex_Digit_Display hex_digit_display_4 (.value(n24h_clock_1_m_lsb));  // open: dp
  Hex_Digit_Display hex_digit_display_5 (.value(n24h_clock_1_s_msb));  // open: dp
  _24H_Clock u_24h_clock_1 (
    .Lpad(Load), .Count(Count), .Clock(clock_1_out), .Clear(Clear), .H_msb(n24h_clock_1_h_msb),
    .H_lsb(n24h_clock_1_h_lsb), .M_msb(n24h_clock_1_m_msb), .M_lsb(n24h_clock_1_m_lsb),
    .S_msb(n24h_clock_1_s_msb), .S_lsb(n24h_clock_1_s_lsb), .in_9(in_4), .in_10(in_5), .in_7(in_6),
    .in_8(in_7), .in_5(in_8), .in_6(in_9));
  Hex_Digit_Display hex_digit_display_6 (.value(n24h_clock_1_s_lsb));  // open: dp
  Hex_Digit_Display hex_digit_display_7 (.value(_60_msb));  // open: dp
  Extra_Logic_Board Busy_Time (.H_msb(n24h_clock_1_h_msb), .H_lsb(n24h_clock_1_h_lsb), .Busy_Time(Busy_Time_busy_time));
  Demultiplexer demultiplexer_1 (
    .out0(demultiplexer_1_out0), .out1(demultiplexer_1_out1), .in(clock_1_out), .sel(Busy_Time_busy_time));  // open: en
  Hex_Digit_Display hex_digit_display_8 (.value(_60_lsb));  // open: dp
  Mod_60_counter _60 (
    .Clock(demultiplexer_1_out1), .Clear(Clear), .MSB(_60_msb), .LSB(_60_lsb), .Next_Clock(_60_next_clock));
  Hex_Digit_Display hex_digit_display_9 (.value(_30_lsb));  // open: dp
  Hex_Digit_Display hex_digit_display_10 (.value(_30_msb));  // open: dp
  Mod_30_counter _30 (
    .Clock(demultiplexer_1_out0), .Clear(Clear), .MSB(_30_msb), .LSB(_30_lsb), .Next_Clock(_30_next_clock));
  and and_1 (and_1_out, _30_next_clock, _60_next_clock);
  not not_1 (not_1_out, and_1_out);
  Mod_4_Up_Counter Mod_4 (.Count(not_1_out), .Clock(clock_1_out), .Clear(Clear), .out_4(Mod_4_out_4));
  LED Right_Turn (.in(traffic_board_1_right_turn__ew));
  LED RED_gREEN (.in(traffic_board_1_straight_ew));
  LED RED_gREEN_2 (.in(traffic_board_1_straight_ns));
  Traffic_Board traffic_board_1 (
    .Input(Mod_4_out_4), .Straight_NS(traffic_board_1_straight_ns),
    .Right_Turn_NS(traffic_board_1_right_turn_ns), .Right_Turn__EW(traffic_board_1_right_turn__ew),
    .Straight_EW(traffic_board_1_straight_ew));
  LED RED_gREEN_3 (.in(traffic_board_1_straight_ns));
  LED Right_Turn_2 (.in(traffic_board_1_right_turn_ns));
  LED Right_Turn_3 (.in(traffic_board_1_right_turn_ns));
  LED Right_Turn_4 (.in(traffic_board_1_right_turn__ew));
  LED RED_gREEN_4 (.in(traffic_board_1_straight_ew));

  // Notes on the sheet:
  //   Hour
  //   Minute
  //   Second
  //   Timer
  //   wEST
  //   North
  //   South
  //   EAST
endmodule
